# Fritzing sketch PCB (saved by Fritzing 0.7.12b)
breadboards: 1

parts:
  U1 = atmega168 [package=dip]
  T1 = LM35 Temperature Sensor [package="TO92 [THT]"]
  S1 = Pushbutton [package="[THT]"]
  S2 = Pushbutton [package="[THT]"]
  LED1 = RGB LED (com. anode, rbg) [package="5 mm [THT]"]
  K1 = Relay [part_number=FRS1B-S package=THT]
  K2 = Relay [part_number=FRS1B-S package=THT]
  U2 = 74HC595 [package="DIP16 [THT]"]  # not connected
  7_Segment1 = 7 Segment Display
  7_Segment2 = 7 Segment Display
  7_Segment3 = 7 Segment Display
  7_Segment4 = 7 Segment Display

nets (from the breadboard view):
  N1: U1.D6_(PWM), LED1.red_cathode, K1.A, K1.B
  N2: U1.D7, LED1.common_anode
  N3: U1.D8, LED1.blue_cathode, K2.A, K2.B
  N4: U1.GND#21, T1.GND, S1.Pin_1, S1.Pin_2, S2.Pin_1, S2.Pin_2, K2.C1, K2.C2
  N5: U1.A1, S1.Pin_3, S1.Pin_4
  N6: U1.A2, S2.Pin_3, S2.Pin_4
  N7: LED1.green_cathode, K1.C1, K1.C2
  N8: K1.COIL1, K1.COIL2
  N9: K2.COIL1, K2.COIL2
  N10: 7_Segment1.Segment_E, 7_Segment1.Segment_D
  N11: 7_Segment1.Segment_DP, 7_Segment1.Segment_C
  N12: 7_Segment2.Segment_E, 7_Segment2.Segment_D
  N13: 7_Segment2.Segment_DP, 7_Segment2.Segment_C
  N14: 7_Segment3.Segment_E, 7_Segment3.Segment_D
  N15: 7_Segment3.Segment_DP, 7_Segment3.Segment_C
  N16: 7_Segment4.Segment_E, 7_Segment4.Segment_D
  N17: 7_Segment4.Segment_DP, 7_Segment4.Segment_C
